# Fritzing sketch rpi_pwm_le (saved by Fritzing 0.9.3b)
breadboards: 1

parts:
  Raspberry_Pi_Zero1 = Raspberry Pi Zero
  R1 = Resistor [tolerance=±5% resistance=330 package=THT]
  LED1 = LED - 3mm [color="Red (635nm)" package="3 mm [THT]"]
  LED2 = LED - 3mm [color="Red (635nm)" package="3 mm [THT]"]
  R2 = Resistor [tolerance=±5% resistance=330 package=THT]

nets:
  N1: Raspberry_Pi_Zero1.GND, LED1.cathode, LED2.cathode
  N2: Raspberry_Pi_Zero1.GIPO16, R1.Pin_0
  N3: Raspberry_Pi_Zero1.GIPO12, R2.Pin_0
  N4: R1.Pin_1, LED1.anode
  N5: LED2.anode, R2.Pin_1
